# Fritzing sketch semiot-device-mcs (saved by Fritzing 0.9.3b)
breadboards: 1

parts:
  LED1 = LED - 5mm [color="Green (570nm)" package="5 mm [THT]"]
  LED2 = LED - 5mm [color="Orange (620nm)" package="5 mm [THT]"]
  LED3 = LED - 5mm [color="Red (633nm)" package="5 mm [THT]"]
  S1 = Toggle Switch [package=THT]
  WeMos_D1_Mini1 = WeMos D1 Mini
  R1 = Resistor [tolerance=±5% resistance=1k package=THT]
  R2 = Resistor [tolerance=±5% resistance=10k package=THT]

nets:
  N1: LED1.cathode, LED2.cathode, LED3.cathode, WeMos_D1_Mini1.G, R1.Pin_0
  N2: LED1.anode, WeMos_D1_Mini1.D1
  N3: LED2.anode, WeMos_D1_Mini1.D2
  N4: LED3.anode, WeMos_D1_Mini1.D3
  N5: S1.COM, WeMos_D1_Mini1.D7, R1.Pin_1
  N6: S1.L2, WeMos_D1_Mini1.D6, R2.Pin_1
  N7: WeMos_D1_Mini1.D5, R2.Pin_0

notes:
  impulse output
